# Fritzing sketch GPS Speedometer (saved by Fritzing 0.9.3b)
breadboards: 1

parts:
  BN-220 = bn-220- GPS-module
  Arduino_Nano_33_IoT = Arduino Nano 33 IOT-tht
  OLED_I2C1 = OLED 128x64 I2C Monochrome Display
  Speeding_LED = LED - 3mm [color="Red (633nm)" package="3 mm [THT]"]
  WiFi_LED = LED - 3mm [color="Red (633nm)" package="3 mm [THT]"]

nets:
  N1: BN-220.pin_1, BN-220.pin_2, BN-220.pin_3, Arduino_Nano_33_IoT.pin_17
  N2: BN-220.pin_4, Arduino_Nano_33_IoT.pin_16
  N3: Arduino_Nano_33_IoT.pin_1, WiFi_LED.anode
  N4: Arduino_Nano_33_IoT.pin_2, OLED_I2C1.VDD
  N5: Arduino_Nano_33_IoT.pin_8, OLED_I2C1.SDA
  N6: Arduino_Nano_33_IoT.pin_9, OLED_I2C1.SCK
  N7: Arduino_Nano_33_IoT.pin_13, Arduino_Nano_33_IoT.pin_18
  N8: Arduino_Nano_33_IoT.pin_14, Arduino_Nano_33_IoT.pin_19, OLED_I2C1.GND, Speeding_LED.cathode, WiFi_LED.cathode
  N9: Arduino_Nano_33_IoT.pin_30, Speeding_LED.anode

custom parts:
  bn-220- GPS-module: bn-220l GPS module. Chipset : 8030-KT Receiving Format : GPS,GLONASS,Galileo,BeiDou,QZSS and SBAS
  Arduino Nano 33 IOT-tht: The Arduino Nano 33 IoT is the easiest and cheapest point of entry to enhance existing devices (and creating new ones) to be part of the IoT and designing pico-network applications. Whether you are looking at building a sensor network connected to your office or home router, or if you want to create a BLE device sending data to a cellphone, the Nano 33 IoT is your one-stop-solution for many of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
